# Fritzing sketch Raspberry Pi RC Car (saved by Fritzing 0.9.4)

parts:
  Raspberry_Pi_1 = Raspberry Pi 3 [part_number=RPI-3-V1.2]
  S1 = H-Bridge with L298N
  M1 = DC Motor
  M2 = DC Motor
  JACK1 = 2.1mm DC Barrel Jack

nets:
  N1: Raspberry_Pi_1.GND, S1.ENA, S1.IN2, S1.IN3
  N2: Raspberry_Pi_1.GPIO17, S1.IN4
  N3: Raspberry_Pi_1.GPIO27, S1.ENB
  N4: Raspberry_Pi_1.GPIO24, S1.GND, JACK1.sleeve
  N5: Raspberry_Pi_1.GPIO23, S1.IN1
  5V: Raspberry_Pi_1.5V, S1.5V
  N6: S1.12V, JACK1.center
  N7: S1.M1-01, M2.pin_1
  N8: S1.M1-02, M2.pin_2
  N9: S1.M2-01, M1.pin_2
  N10: S1.M2-02, M1.pin_1

notes:
  12v powersupply ----->
  BO Motor

custom parts:
  H-Bridge with L298N: h-bridge
  2.1mm DC Barrel Jack: 2.1mm DC Barrel Jack with Thru-Hole Connectors (breadboardable)
